# Fritzing sketch Sketch (saved by Fritzing 0.9.3b)
breadboards: 1

parts:
  Composant1 = Arduino Nano (Rev3.0) (ICSP)
  C2 = Electrolytic Capacitor [capacitance=47µF package="0807 [SMD, electrolytic]"]
  Q2 = PNP-Transistor [package="TO92 [THT]"]
  Q3 = NPN-Transistor [package="TO92 [THT]"]
  Q4 = NPN-Transistor [package="TO92 [THT]"]
  Q5 = PNP-Transistor [package="TO92 [THT]"]
  SP1 = SPEAKER [package=pcb_mount_speaker]
  C3 = Electrolytic Capacitor [capacitance=100μF voltage=6.3V package="0807 [SMD, electrolytic]"]

nets:
  GND: Composant1.GND, C2.-, Q2.C, Q5.C
  N1: Composant1.D9, Q2.B, Q3.B
  N2: Composant1.D10, Q4.B, Q5.B
  5V: Composant1.5V, C2.+, Q3.C, Q4.C
  N3: Q2.E, Q3.E, C3.+
  N4: Q4.E, Q5.E, SP1.-
  N5: SP1.+, C3.-
